// Logisim project cpu.circ as structural Verilog: 5 circuits, main circuit main
module main (
  input  [31:0] INSTRUCTION,
  input  CLOCK,
  output [31:0] FETCH_ADDRESS,
  output [31:0] ra,
  output [31:0] sp,
  output [31:0] t0,
  output [31:0] t1,
  output [31:0] t2,
  output [31:0] s0,
  output [31:0] s1,
  output [31:0] a0
);

  wire [2:0] funct3;
  wire [4:0] rd, rs1, rs2;
  wire [6:0] funct7, opcode;
  wire [31:0] adder_1_out;

  split_instruction split_instruction_1 (
    .rd(rd), .opcode(opcode), .rs2(rs2), .funct3(funct3), .OriginalInstruction(INSTRUCTION), .rs1(rs1),
    .funct7(funct7));
  branchcom branchcom_1 ();  // open: DataA, DataB, compare_unsigned, BEQ, BLT
  Adder #(.width(32)) adder_1 (.a(FETCH_ADDRESS), .b(32'h1), .out(adder_1_out));  // open: cin, cout
  Register #(.width(32)) PC (.D(adder_1_out), .clk(CLOCK), .Q(FETCH_ADDRESS));  // open: en, clr
  // alu Arithmetic_Logic_Unit: pin names not known
  // mem_main DMEM: pin names not known
  // regfile_main RegFile: pin names not known

  // Other names for the same wires on the sheet: clk = CLOCK; fetch_addr[31:0] = FETCH_ADDRESS

  // Notes on the sheet:
  //   Output
  //   Inputs/Outputs from run.circ. DO NOT MOVE THESE.
  //   Inputs
  //   Inputs/Outputs from run.circ. DO NOT MOVE THESE.
endmodule

module immgen (
  input  [24:0] B,
  input  [2:0] in_2,
  output [31:0] out_3
);

  wire [31:0] bit_extender_1_out, bit_extender_2_out, bit_extender_3_out, bit_extender_4_out,
       bit_extender_5_out;

  assign bit_extender_1_out = {{20{B[24]}}, B[24:13]};  // Bit_Extender bit_extender_1
  assign bit_extender_2_out = {{20{B[24]}}, {B[24:18], B[4:0]}};  // Bit_Extender bit_extender_2
  assign bit_extender_3_out = {{19{B[24]}}, {B[24], B[0], B[23:18], B[4:1], 1'b0}};  // Bit_Extender bit_extender_3
  assign bit_extender_4_out = {{11{B[24]}}, {B[24], B[12:5], B[13], B[23:14], 1'b0}};  // Bit_Extender bit_extender_4
  assign bit_extender_5_out = {{27{1'b0}}, B[17:13]};  // Bit_Extender bit_extender_5
  Multiplexer #(.select(3), .width(32), .enable("false")) multiplexer_1 (
    .in0(bit_extender_1_out), .in1(bit_extender_2_out), .in2(bit_extender_3_out),
    .in3({B[24:5], {12{1'b0}}}), .in4(bit_extender_4_out), .in5(bit_extender_5_out), .out(out_3), .sel(in_2));  // open: in6, in7

  // Notes on the sheet:
  //   I
  //   S
  //   U
  //   J
  //   other
endmodule

module branchcom (
  input  [31:0] DataA,
  input  [31:0] DataB,
  input  compare_unsigned,
  output BEQ,
  output BLT
);

  wire comparator_1_eq, comparator_1_lt, comparator_2_eq, comparator_2_lt;

  Comparator #(.width(32)) comparator_1 (.a(DataA), .b(DataB), .eq(comparator_1_eq), .lt(comparator_1_lt));  // open: gt
  Comparator #(.width(32), .mode("unsigned")) comparator_2 (
    .a(DataA), .b(DataB), .eq(comparator_2_eq), .lt(comparator_2_lt));  // open: gt
  Multiplexer #(.enable("false")) multiplexer_1 (
    .in0(comparator_1_eq), .in1(comparator_2_eq), .out(BEQ), .sel(compare_unsigned));
  Multiplexer #(.enable("false")) multiplexer_2 (
    .in0(comparator_1_lt), .in1(comparator_2_lt), .out(BLT), .sel(compare_unsigned));
endmodule

module split_instruction (
  input  [31:0] OriginalInstruction,
  output [6:0] opcode,
  output [4:0] rd,
  output [2:0] funct3,
  output [4:0] rs1,
  output [4:0] rs2,
  output [6:0] funct7
);


  assign funct3 = OriginalInstruction[14:12];
  assign funct7 = OriginalInstruction[31:25];
  assign opcode = OriginalInstruction[6:0];
  assign rd = OriginalInstruction[11:7];
  assign rs1 = OriginalInstruction[19:15];
  assign rs2 = OriginalInstruction[24:20];
endmodule

module parse_instruction (
  input  [6:0] funct7,
  input  [2:0] funct3,
  input  [6:0] opcode
);

  wire add0, addi0, and0, andi0, auipc0, beq0, bgeu0, blt0, bltu0, bne0, BrUn, comparator_10_eq,
       comparator_11_eq, comparator_12_eq, comparator_13_eq, comparator_14_eq, comparator_15_eq,
       comparator_16_eq, comparator_17_eq, comparator_18_eq, comparator_19_eq, comparator_20_eq,
       comparator_21_eq, comparator_22_eq, comparator_23_eq, comparator_24_eq, comparator_25_eq,
       comparator_26_eq, comparator_27_eq, comparator_28_eq, comparator_29_eq, comparator_30_eq,
       comparator_31_eq, comparator_32_eq, comparator_33_eq, comparator_34_eq, comparator_35_eq,
       comparator_36_eq, comparator_37_eq, comparator_38_eq, comparator_39_eq, comparator_40_eq,
       comparator_41_eq, comparator_42_eq, comparator_43_eq, comparator_44_eq, comparator_45_eq,
       comparator_46_eq, comparator_47_eq, comparator_48_eq, comparator_49_eq, comparator_50_eq,
       comparator_51_eq, comparator_52_eq, comparator_53_eq, comparator_54_eq, div0, divu0,
       I_type_instruction, jal0, jalr0, lb0, lbu0, lh0, lhu0, Load_instruction, lui0, lw0, mul0, mulh0,
       mulhu0, or0, or_2_out, ori0, R_type_instruction, RegWEn, remu0, SB_type_instruction, sll0, slli0,
       slti0, srl0, srli0, sub0, sw0, xor0, xori0;

  Comparator #(.width(7)) comparator_1 (.a(opcode), .b(7'b0110011), .eq(R_type_instruction));  // open: gt, lt
  Comparator #(.width(7)) comparator_2 (.a(opcode), .b(7'b0000011), .eq(Load_instruction));  // open: gt, lt
  Comparator #(.width(7)) comparator_3 (.a(opcode), .b(7'b0010011), .eq(I_type_instruction));  // open: gt, lt
  Comparator #(.width(7)) comparator_4 (.a(opcode), .b(7'b0100011), .eq(sw0));  // open: gt, lt
  Comparator #(.width(7)) comparator_5 (.a(opcode), .b(7'b1100011), .eq(SB_type_instruction));  // open: gt, lt
  Comparator #(.width(7)) comparator_6 (.a(opcode), .b(7'b0010111), .eq(auipc0));  // open: gt, lt
  Comparator #(.width(7)) comparator_7 (.a(opcode), .b(7'b0110111), .eq(lui0));  // open: gt, lt
  Comparator #(.width(7)) comparator_8 (.a(opcode), .b(7'b1101111), .eq(jal0));  // open: gt, lt
  Comparator #(.width(7)) comparator_9 (.a(opcode), .b(7'b1100111), .eq(jalr0));  // open: gt, lt
  or or_1 (BrUn, bltu0, bgeu0);
  or or_2 (or_2_out, SB_type_instruction, sw0);
  not not_1 (RegWEn, or_2_out);
  Comparator #(.width(3)) comparator_10 (.a(funct3), .b(3'b000), .eq(comparator_10_eq));  // open: gt, lt
  Comparator #(.width(7)) comparator_11 (.a(funct7), .b({7{1'b0}}), .eq(comparator_11_eq));  // open: gt, lt
  Comparator #(.width(3)) comparator_12 (.a(funct3), .b(3'b000), .eq(comparator_12_eq));  // open: gt, lt
  Comparator #(.width(7)) comparator_13 (.a(funct7), .b(7'b0000001), .eq(comparator_13_eq));  // open: gt, lt
  Comparator #(.width(3)) comparator_14 (.a(funct3), .b(3'b000), .eq(comparator_14_eq));  // open: gt, lt
  Comparator #(.width(7)) comparator_15 (.a(funct7), .b(7'b0100000), .eq(comparator_15_eq));  // open: gt, lt
  Comparator #(.width(3)) comparator_16 (.a(funct3), .b(3'b111), .eq(comparator_16_eq));  // open: gt, lt
  Comparator #(.width(7)) comparator_17 (.a(funct7), .b({7{1'b0}}), .eq(comparator_17_eq));  // open: gt, lt
  Comparator #(.width(3)) comparator_18 (.a(funct3), .b(3'b100), .eq(comparator_18_eq));  // open: gt, lt
  Comparator #(.width(3)) comparator_19 (.a(funct3), .b(3'b010), .eq(comparator_19_eq));  // open: gt, lt
  Comparator #(.width(3)) comparator_20 (.a(funct3), .b(3'b111), .eq(comparator_20_eq));  // open: gt, lt
  Comparator #(.width(3)) comparator_21 (.a(funct3), .b(3'b001), .eq(comparator_21_eq));  // open: gt, lt
  and and_1 (add0, comparator_10_eq, comparator_11_eq, R_type_instruction);
  and and_2 (mul0, comparator_12_eq, comparator_13_eq, R_type_instruction);
  and and_3 (sub0, comparator_14_eq, comparator_15_eq, R_type_instruction);
  and and_4 (and0, comparator_16_eq, comparator_17_eq, R_type_instruction);
  and and_5 (lbu0, comparator_18_eq, Load_instruction);
  and and_6 (slti0, comparator_19_eq, I_type_instruction);
  and and_7 (andi0, comparator_20_eq, I_type_instruction);
  and and_8 (bne0, comparator_21_eq, SB_type_instruction);
  Comparator #(.width(3)) comparator_22 (.a(funct3), .b(3'b001), .eq(comparator_22_eq));  // open: gt, lt
  Comparator #(.width(7)) comparator_23 (.a(funct7), .b({7{1'b0}}), .eq(comparator_23_eq));  // open: gt, lt
  Comparator #(.width(3)) comparator_24 (.a(funct3), .b(3'b001), .eq(comparator_24_eq));  // open: gt, lt
  Comparator #(.width(7)) comparator_25 (.a(funct7), .b(7'b0000001), .eq(comparator_25_eq));  // open: gt, lt
  Comparator #(.width(3)) comparator_26 (.a(funct3), .b(3'b011), .eq(comparator_26_eq));  // open: gt, lt
  Comparator #(.width(7)) comparator_27 (.a(funct7), .b(7'b0000001), .eq(comparator_27_eq));  // open: gt, lt
  Comparator #(.width(3)) comparator_28 (.a(funct3), .b(3'b000), .eq(comparator_28_eq));  // open: gt, lt
  Comparator #(.width(3)) comparator_29 (.a(funct3), .b(3'b101), .eq(comparator_29_eq));  // open: gt, lt
  Comparator #(.width(3)) comparator_30 (.a(funct3), .b(3'b100), .eq(comparator_30_eq));  // open: gt, lt
  Comparator #(.width(3)) comparator_31 (.a(funct3), .b(3'b000), .eq(comparator_31_eq));  // open: gt, lt
  Comparator #(.width(3)) comparator_32 (.a(funct3), .b(3'b111), .eq(comparator_32_eq));  // open: gt, lt
  and and_9 (sll0, comparator_22_eq, comparator_23_eq, R_type_instruction);
  and and_10 (mulh0, comparator_24_eq, comparator_25_eq, R_type_instruction);
  and and_11 (mulhu0, comparator_26_eq, comparator_27_eq, R_type_instruction);
  and and_12 (lb0, comparator_28_eq, Load_instruction);
  and and_13 (lhu0, comparator_29_eq, Load_instruction);
  and and_14 (xori0, comparator_30_eq, I_type_instruction);
  and and_15 (beq0, comparator_31_eq, SB_type_instruction);
  and and_16 (bgeu0, comparator_32_eq, SB_type_instruction);
  Comparator #(.width(3)) comparator_33 (.a(funct3), .b(3'b100), .eq(comparator_33_eq));  // open: gt, lt
  Comparator #(.width(7)) comparator_34 (.a(funct7), .b({7{1'b0}}), .eq(comparator_34_eq));  // open: gt, lt
  Comparator #(.width(3)) comparator_35 (.a(funct3), .b(3'b100), .eq(comparator_35_eq));  // open: gt, lt
  Comparator #(.width(7)) comparator_36 (.a(funct7), .b(7'b0010000), .eq(comparator_36_eq));  // open: gt, lt
  Comparator #(.width(3)) comparator_37 (.a(funct3), .b(3'b101), .eq(comparator_37_eq));  // open: gt, lt
  Comparator #(.width(7)) comparator_38 (.a(funct7), .b(7'b0000001), .eq(comparator_38_eq));  // open: gt, lt
  Comparator #(.width(3)) comparator_39 (.a(funct3), .b(3'b001), .eq(comparator_39_eq));  // open: gt, lt
  Comparator #(.width(3)) comparator_40 (.a(funct3), .b(3'b000), .eq(comparator_40_eq));  // open: gt, lt
  Comparator #(.width(3)) comparator_41 (.a(funct3), .b(3'b101), .eq(comparator_41_eq));  // open: gt, lt
  Comparator #(.width(7)) comparator_42 (.a(funct7), .b({7{1'b0}}), .eq(comparator_42_eq));  // open: gt, lt
  Comparator #(.width(3)) comparator_43 (.a(funct3), .b(3'b100), .eq(comparator_43_eq));  // open: gt, lt
  and and_17 (xor0, comparator_33_eq, comparator_34_eq, R_type_instruction);
  and and_18 (div0, comparator_35_eq, comparator_36_eq, R_type_instruction);
  and and_19 (divu0, comparator_37_eq, comparator_38_eq, R_type_instruction);
  and and_20 (lh0, comparator_39_eq, Load_instruction);
  and and_21 (addi0, comparator_40_eq, I_type_instruction);
  and and_22 (srli0, comparator_41_eq, comparator_42_eq, I_type_instruction);
  and and_23 (blt0, comparator_43_eq, SB_type_instruction);
  Comparator #(.width(3)) comparator_44 (.a(funct3), .b(3'b101), .eq(comparator_44_eq));  // open: gt, lt
  Comparator #(.width(7)) comparator_45 (.a(funct7), .b({7{1'b0}}), .eq(comparator_45_eq));  // open: gt, lt
  Comparator #(.width(3)) comparator_46 (.a(funct3), .b(3'b110), .eq(comparator_46_eq));  // open: gt, lt
  Comparator #(.width(7)) comparator_47 (.a(funct7), .b({7{1'b0}}), .eq(comparator_47_eq));  // open: gt, lt
  Comparator #(.width(3)) comparator_48 (.a(funct3), .b(3'b111), .eq(comparator_48_eq));  // open: gt, lt
  Comparator #(.width(7)) comparator_49 (.a(funct7), .b(7'b0000001), .eq(comparator_49_eq));  // open: gt, lt
  Comparator #(.width(3)) comparator_50 (.a(funct3), .b(3'b010), .eq(comparator_50_eq));  // open: gt, lt
  Comparator #(.width(3)) comparator_51 (.a(funct3), .b(3'b001), .eq(comparator_51_eq));  // open: gt, lt
  Comparator #(.width(7)) comparator_52 (.a(funct7), .b({7{1'b0}}), .eq(comparator_52_eq));  // open: gt, lt
  Comparator #(.width(3)) comparator_53 (.a(funct3), .b(3'b110), .eq(comparator_53_eq));  // open: gt, lt
  Comparator #(.width(3)) comparator_54 (.a(funct3), .b(3'b110), .eq(comparator_54_eq));  // open: gt, lt
  and and_24 (srl0, comparator_44_eq, comparator_45_eq, R_type_instruction);
  and and_25 (or0, comparator_46_eq, comparator_47_eq, R_type_instruction);
  and and_26 (remu0, comparator_48_eq, comparator_49_eq, R_type_instruction);
  and and_27 (lw0, comparator_50_eq, Load_instruction);
  and and_28 (slli0, comparator_51_eq, comparator_52_eq, I_type_instruction);
  and and_29 (ori0, comparator_53_eq, I_type_instruction);
  and and_30 (bltu0, comparator_54_eq, SB_type_instruction);
endmodule
